# Fritzing sketch softbot (saved by Fritzing 0.9.3b)

parts:
  Teensy1 = Teensy 3.6 (Basic)  # not connected
  Part1 = POLOLU 713 Motor Driver 1A Dual TB6612FNG
  Arm = Soft Actuator
  VALVE2 = Plastic Solenoid Valve
  VALVE1 = Plastic Solenoid Valve
  Arm_2 = Soft Actuator
  VALVE3 = Plastic Solenoid Valve
  VALVE4 = Plastic Solenoid Valve
  Part2 = POLOLU 713 Motor Driver 1A Dual TB6612FNG
  Neck = Soft Actuator
  VALVE5 = Plastic Solenoid Valve
  VALVE6 = Plastic Solenoid Valve
  Part3 = POLOLU 713 Motor Driver 1A Dual TB6612FNG
  Neck_2 = Soft Actuator
  VALVE7 = Plastic Solenoid Valve
  VALVE8 = Plastic Solenoid Valve
  Part4 = POLOLU 713 Motor Driver 1A Dual TB6612FNG
  Neck_3 = Soft Actuator
  VALVE9 = Plastic Solenoid Valve
  VALVE10 = Plastic Solenoid Valve
  Part5 = POLOLU 713 Motor Driver 1A Dual TB6612FNG

nets:
  N1: Part1.BO1, VALVE1.O1
  N2: Part1.BO2, VALVE1.O2
  N3: Part1.AO2, VALVE2.O2
  N4: Part1.AO1, VALVE2.O1
  N5: Arm.Inlet, VALVE2.Outlet
  N6: Arm_2.Inlet, VALVE4.Outlet
  N7: VALVE3.O1, Part2.BO1
  N8: VALVE3.O2, Part2.BO2
  N9: VALVE4.O1, Part2.AO2
  N10: VALVE4.O2, Part2.AO1
  N11: Neck.Inlet, VALVE6.Outlet
  N12: VALVE5.O1, Part3.BO1
  N13: VALVE5.O2, Part3.BO2
  N14: VALVE6.O1, Part3.AO2
  N15: VALVE6.O2, Part3.AO1
  N16: Neck_2.Inlet, VALVE8.Outlet
  N17: VALVE7.O1, Part4.BO1
  N18: VALVE7.O2, Part4.BO2
  N19: VALVE8.O1, Part4.AO2
  N20: VALVE8.O2, Part4.AO1
  N21: Neck_3.Inlet, VALVE10.Outlet
  N22: VALVE9.O1, Part5.BO1
  N23: VALVE9.O2, Part5.BO2
  N24: VALVE10.O1, Part5.AO2

custom parts:
  Teensy 3.6 (Basic): The Teensy is a complete USB-based microcontoller development system, in a very small footprint, capable of implementing many types of projects. All programming is done via the USB port. No special programmer is needed, only a standard micro-USB cable and a PC or Macintosh with a USB port.
  POLOLU 713 Motor Driver 1A Dual TB6612FNG: The TB6612FNG motor driver can control up to two DC motors at a constant current of 1.2A (3.2A peak). Two input signals (IN1 and IN2) can be used to control the motor in one of four function modes - CW, CCW, short-brake, and stop. The two motor outputs (A and B) can be separately controlled, the speed of each motor is controlled via a PWM input signal with a frequency up to 100kHz. The STBY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
